// Logisim project SAP1.circ as structural Verilog: 21 circuits, main circuit reg_gp
module main (
  input  in_1,
  input  in_2,
  input  in_3,
  input  in_4,
  input  in_5,
  input  in_6,
  output out_7,
  output out_8,
  output out_9,
  output [3:0] out_10,
  output [7:0] out_11,
  output out_12,
  output [7:0] out_13,
  output out_14,
  output [7:0] out_15,
  output out_16,
  output out_17,
  output out_18,
  output out_19,
  output [7:0] out_20,
  output [7:0] out_21,
  output out_22,
  output [7:0] out_23,
  output [7:0] out_24,
  output [7:0] out_25,
  output out_26,
  output [7:0] out_27,
  output [7:0] out_28,
  output [7:0] out_29,
  output out_30,
  output [7:0] out_31,
  output [7:0] out_32,
  output [7:0] out_33,
  output [7:0] out_34,
  output [3:0] out_35,
  output [7:0] out_36,
  output [3:0] out_37,
  output [7:0] out_38,
  output out_39,
  output [7:0] out_40,
  output [7:0] out_41,
  output [7:0] out_42,
  output out_43,
  output [3:0] out_44,
  output out_45,
  output out_46,
  output out_47,
  output out_48,
  output out_49,
  output out_50,
  output out_51,
  output [3:0] out_52,
  output out_53,
  output [7:0] out_54,
  output out_55,
  output out_56,
  output out_57,
  output out_58,
  output out_59,
  output out_60
);

  wire a_in, a_out, alu_out, alu_out_en, alu_sub, and_1_out, and_2_out, b_in, cont_seqqq_1_hlt,
       cont_seqqq_1_t1, cont_seqqq_1_t2, cont_seqqq_1_t3, cont_seqqq_1_t4, cont_seqqq_1_t5, cont_seqqq_1_t6,
       controlled_buffer_3_out, ins_reg_in_en, ins_reg_out_en, mar_in_en, new_reg_in, new_reg_out, pc_en,
       pc_out, reg_a_out_en, rot_am, rot_dir, rot_in, rot_out, rot_out_en, rot_reg_in_en, sft_am, sft_dir,
       sft_in, sft_out, sft_out_en, sft_reg_in_en, sram_rd, sram_wr, t1, t2;
  wire [3:0] alu_2_1_alu_output, alu_2_1_alu_output_2, alu_2_1_rotate_output, alu_2_1_rotate_output_2,
       alu_2_1_shift_output, alu_2_1_shift_output_2, controlled_buffer_6_out, controlled_buffer_7_out,
       data_loader_1_out_6, new_reg_1_reg_int_out, new_reg_1_reg_out, undriven;
  wire [7:0] controlled_buffer_4_out, controlled_buffer_5_out, multiplexer_1_out, reg_gp_1_reg_out;

  Multiplexer #(.width(8)) multiplexer_1 (.in0(out_15), .in1({undriven, out_52}), .out(multiplexer_1_out), .sel(in_5));
  Hex_Digit_Display hex_digit_display_1 (.value(out_10));  // open: dp
  prog_counter prog_counter_1 (
    .pc_en(pc_en), .clk(in_3), .pc_reset(in_4), .pc_out_en(pc_out), .pc_value(out_10), .pc_output(out_15[3:0]));
  Hex_Digit_Display hex_digit_display_2 (.value(out_15[7:4]));  // open: dp
  Hex_Digit_Display hex_digit_display_3 (.value(out_15[3:0]));  // open: dp
  ram_cir ram_cir_1 (
    .sram_rd(sram_rd), .sram_wr(sram_wr), .sram_d_in(out_15), .mar_d_in(multiplexer_1_out),
    .mar_in_en(mar_in_en), .sram_clk(in_3), .sram_d_out(out_15), .out_8(out_21), .out_9(out_23),
    .out_10(out_24), .out_11(out_25), .out_12(out_27), .out_13(out_28), .out_14(out_29), .out_15(out_31),
    .out_16(out_32), .out_17(out_33), .out_18(out_34), .out_19(out_36), .out_20(out_38), .out_21(out_40),
    .out_22(out_41), .out_23(out_42));
  Hex_Digit_Display hex_digit_display_4 (.value(out_52));  // open: dp
  data_loader data_loader_1 (
    .clk(in_3), .reset(in_4), .enable(in_1), .debug(in_5), .address(out_52), .out_6(data_loader_1_out_6),
    .data(out_54), .t1(t1), .t2(t2), .mar_in_en(mar_in_en), .sram_wr(sram_wr));
  Hex_Digit_Display hex_digit_display_5 (.value(out_15[7:4]));  // open: dp
  LED led_1 (.in(and_1_out));
  and and_1 (and_1_out, in_1, in_5);
  Hex_Digit_Display hex_digit_display_6 (.value(out_15[3:0]));  // open: dp
  Hex_Digit_Display hex_digit_display_7 (.value(out_54[7:4]));  // open: dp
  Hex_Digit_Display hex_digit_display_8 (.value(out_54[3:0]));  // open: dp
  assign out_15 = in_5 ? out_54 : 8'bz;  // Controlled_Buffer controlled_buffer_1
  LED led_2 (.in(in_3));
  and and_2 (and_2_out, in_3, cont_seqqq_1_hlt);
  assign out_15 = reg_a_out_en ? out_11 : 8'bz;  // Controlled_Buffer controlled_buffer_2
  assign controlled_buffer_3_out = in_2 ? and_2_out : 1'bz;  // Controlled_Buffer controlled_buffer_3
  LED led_3 (.in(in_2));
  Hex_Digit_Display hex_digit_display_9 (.value(out_11[7:4]));  // open: dp
  reg_gp reg_gp_1 (
    .reg_in(out_15), .reg_in_en(a_in), .reg_clk(in_3), .reg_out_en(a_out), .reg_int_out(out_11),
    .reg_out(reg_gp_1_reg_out));
  reg_gp reg_gp_2 (
    .reg_in(out_15), .reg_in_en(b_in), .reg_clk(in_3), .reg_out_en(in_6), .reg_int_out(out_20),
    .reg_out(reg_gp_1_reg_out));
  Hex_Digit_Display hex_digit_display_10 (.value(out_20[7:4]));  // open: dp
  ins_reg ins_reg_1 (
    .ins_reg_in(out_15), .ins_reg_in_en(ins_reg_in_en), .clk(in_3), .ins_reg_out_en(ins_reg_out_en),
    .add_outs(out_15[3:0]), .ins_out(out_37));
  Hex_Digit_Display hex_digit_display_11 (.value(out_11[3:0]));  // open: dp
  Hex_Digit_Display hex_digit_display_12 (.value(out_20[3:0]));  // open: dp
  Hex_Digit_Display hex_digit_display_13 (.value(out_37), .dp(out_37[0]));
  Hex_Digit_Display hex_digit_display_14 (.value(out_13[7:4]));  // open: dp
  Hex_Digit_Display hex_digit_display_15 (.value(out_13[3:0]));  // open: dp
  cont_seqqq cont_seqqq_1 (
    .clk(controlled_buffer_3_out), .CLR(in_4), .dec_sel(out_37), .en(in_2), .T6(cont_seqqq_1_t6),
    .T5(cont_seqqq_1_t5), .T4(cont_seqqq_1_t4), .T3(cont_seqqq_1_t3), .T2(cont_seqqq_1_t2),
    .T1(cont_seqqq_1_t1), .ins_reg_out_en(ins_reg_out_en), .a_in(a_in), .b_in(b_in), .add_out(alu_out),
    .sub_out(alu_sub), .sram_wr(sram_wr), .alu_out_en(alu_out_en), .sft_dir(sft_dir), .rot_dir(rot_dir),
    .pc_en(pc_en), .mar_in_en(mar_in_en), .pc_out(pc_out), .sram_rd(sram_rd), .ins_reg_in_en(ins_reg_in_en),
    .new_reg_in(new_reg_in), .new_reg_out(new_reg_out), .a_out(a_out), .sft_am(sft_am), .rot_am(rot_am),
    .sft_in(sft_in), .rot_in(rot_in), .sft_out_en(sft_out_en), .rot_out_en(rot_out_en), .sft_out(sft_out),
    .rot_out(rot_out), .sft_reg_in_en(sft_reg_in_en), .rot_reg_in_en(rot_reg_in_en),
    .reg_a_out_en(reg_a_out_en), .HLT(cont_seqqq_1_hlt));
  Hex_Digit_Display hex_digit_display_16 (.value(out_15[3:0]));  // open: dp
  assign controlled_buffer_4_out = sft_in ? out_11 : 8'bz;  // Controlled_Buffer controlled_buffer_4
  assign controlled_buffer_5_out = rot_in ? out_11 : 8'bz;  // Controlled_Buffer controlled_buffer_5
  new_reg new_reg_1 (
    .reg_in(out_15[3:0]), .reg_in_en(new_reg_in), .reg_clk(in_3), .reg_out_en(new_reg_out),
    .reg_int_out(new_reg_1_reg_int_out), .reg_out(new_reg_1_reg_out));
  Hex_Digit_Display hex_digit_display_17 (.value({1'b0, out_44[2:0]}));  // open: dp
  assign controlled_buffer_6_out = sft_am ? new_reg_1_reg_out : 4'bz;  // Controlled_Buffer controlled_buffer_6
  assign controlled_buffer_7_out = rot_am ? new_reg_1_reg_out : 4'bz;  // Controlled_Buffer controlled_buffer_7
  Hex_Digit_Display hex_digit_display_18 (.value(new_reg_1_reg_out));  // open: dp
  Hex_Digit_Display hex_digit_display_19 (.value(new_reg_1_reg_int_out));  // open: dp
  Hex_Digit_Display hex_digit_display_20 (.value(alu_2_1_alu_output_2));  // open: dp
  Hex_Digit_Display hex_digit_display_21 (.value(alu_2_1_alu_output));  // open: dp
  alu_2 alu_2_1 (
    .reg_a(out_11), .alu_out(alu_out), .alu_sub(alu_sub), .reg_b(out_20),
    .shift_in_data(controlled_buffer_4_out), .shift_direction(sft_dir), .sft_reg_in_en(sft_reg_in_en),
    .shift_amount(controlled_buffer_6_out), .sft_out(sft_out), .clk(in_3),
    .rotate_in_data(controlled_buffer_5_out), .rotate_direction(rot_dir), .rot_reg_in_en(rot_reg_in_en),
    .rotate_amount(controlled_buffer_7_out), .rot_out(rot_out),
    .alu_output({alu_2_1_alu_output_2, alu_2_1_alu_output}),
    .shift_output({alu_2_1_shift_output_2, alu_2_1_shift_output}),
    .rotate_output({alu_2_1_rotate_output_2, alu_2_1_rotate_output}));  // open: alu_carry_out
  T_states t_states_1 (
    .T6(cont_seqqq_1_t6), .T5(cont_seqqq_1_t5), .T4(cont_seqqq_1_t4), .T3(cont_seqqq_1_t3),
    .T2(cont_seqqq_1_t2), .T1(cont_seqqq_1_t1), .O1(out_44[0]), .O2(out_44[1]), .O3(out_44[2]));
  Hex_Digit_Display hex_digit_display_22 (.value(alu_2_1_shift_output_2));  // open: dp
  assign out_15 = alu_out_en ? {alu_2_1_alu_output_2, alu_2_1_alu_output} : 8'bz;  // Controlled_Buffer controlled_buffer_8
  assign out_15 = rot_out_en ? {alu_2_1_rotate_output_2, alu_2_1_rotate_output} : 8'bz;  // Controlled_Buffer controlled_buffer_9
  Hex_Digit_Display hex_digit_display_23 (.value(alu_2_1_shift_output));  // open: dp
  Hex_Digit_Display hex_digit_display_24 (.value(alu_2_1_rotate_output_2));  // open: dp
  assign out_15 = sft_out_en ? {alu_2_1_shift_output_2, alu_2_1_shift_output} : 8'bz;  // Controlled_Buffer controlled_buffer_10
  Hex_Digit_Display hex_digit_display_25 (.value(alu_2_1_rotate_output));  // open: dp
  assign out_47 = in_2 ? sram_rd : 1'bz;  // Controlled_Buffer controlled_buffer_11
  assign out_50 = in_2 ? a_in : 1'bz;  // Controlled_Buffer controlled_buffer_12
  assign out_51 = in_2 ? a_out : 1'bz;  // Controlled_Buffer controlled_buffer_13
  assign out_55 = in_2 ? b_in : 1'bz;  // Controlled_Buffer controlled_buffer_14
  assign out_56 = in_2 ? alu_out : 1'bz;  // Controlled_Buffer controlled_buffer_15
  assign out_57 = in_2 ? alu_sub : 1'bz;  // Controlled_Buffer controlled_buffer_16
  assign out_7 = in_2 ? sft_in : 1'bz;  // Controlled_Buffer controlled_buffer_17
  assign out_8 = in_2 ? sft_am : 1'bz;  // Controlled_Buffer controlled_buffer_18
  assign out_9 = in_2 ? sft_dir : 1'bz;  // Controlled_Buffer controlled_buffer_19
  assign out_12 = in_2 ? sft_out_en : 1'bz;  // Controlled_Buffer controlled_buffer_20
  assign out_14 = in_2 ? sft_out : 1'bz;  // Controlled_Buffer controlled_buffer_21
  assign out_16 = in_2 ? sft_reg_in_en : 1'bz;  // Controlled_Buffer controlled_buffer_22
  assign out_17 = in_2 ? rot_in : 1'bz;  // Controlled_Buffer controlled_buffer_23
  assign out_18 = in_2 ? rot_am : 1'bz;  // Controlled_Buffer controlled_buffer_24
  assign out_19 = in_2 ? rot_dir : 1'bz;  // Controlled_Buffer controlled_buffer_25
  assign out_22 = in_2 ? rot_out_en : 1'bz;  // Controlled_Buffer controlled_buffer_26
  assign out_26 = in_2 ? rot_out : 1'bz;  // Controlled_Buffer controlled_buffer_27
  assign out_30 = in_2 ? rot_reg_in_en : 1'bz;  // Controlled_Buffer controlled_buffer_28
  assign out_39 = in_2 ? new_reg_in : 1'bz;  // Controlled_Buffer controlled_buffer_29
  assign out_43 = in_2 ? new_reg_out : 1'bz;  // Controlled_Buffer controlled_buffer_30
  assign out_45 = in_2 ? pc_en : 1'bz;  // Controlled_Buffer controlled_buffer_31
  assign out_46 = in_2 ? pc_out : 1'bz;  // Controlled_Buffer controlled_buffer_32
  assign out_48 = in_2 ? sram_wr : 1'bz;  // Controlled_Buffer controlled_buffer_33
  assign out_49 = in_2 ? mar_in_en : 1'bz;  // Controlled_Buffer controlled_buffer_34
  assign out_53 = in_2 ? reg_a_out_en : 1'bz;  // Controlled_Buffer controlled_buffer_35
  assign out_58 = in_2 ? alu_out_en : 1'bz;  // Controlled_Buffer controlled_buffer_36
  assign out_59 = in_2 ? ins_reg_in_en : 1'bz;  // Controlled_Buffer controlled_buffer_37
  assign out_60 = in_2 ? ins_reg_out_en : 1'bz;  // Controlled_Buffer controlled_buffer_38
  // Pins of 1 and 4 bits meet at out_37

  assign out_35 = out_15[3:0];
  assign out_44[3] = 1'b0;

  // Other names for the same wires on the sheet: address[3:0] = out_52; b_out = in_6; clk = in_3; data_load_en = in_1;
  //   debug = in_5; debug_data[7:0] = out_54; en = in_2; pc_reset = in_4

  // Notes on the sheet:
  //   PC
  //   Data Loader
  //   RAM
  //   Data loading
  //   Clock
  //   Reg A
  //   Reg B
  //   IR
  //   Operation
  //   Control Sequencer
  //   Sft/Rot Amount Reg
  //   Total ALU
  //   T States
  //   SHIFT
  //   ROTATE
  //   PC CONTROLLER
  //   IR CONTROLLER
  //   MEMORY CONTROLLER
  //   REG A CONTROLLER
  //   REG B CONTROLLER
  //   ALU CONTROLLER
  //   Sft/Rot Amount Reg CONTROLLER
endmodule

module reg_gp (
  input  [7:0] reg_in,
  input  reg_in_en,
  input  reg_clk,
  input  reg_out_en,
  output [7:0] reg_int_out,
  output [7:0] reg_out
);

  wire multiplexer_1_out, multiplexer_2_out, multiplexer_3_out, multiplexer_4_out, multiplexer_5_out,
       multiplexer_6_out, multiplexer_7_out, multiplexer_8_out;

  Multiplexer multiplexer_1 (.in0(reg_int_out[7]), .in1(reg_in[7]), .out(multiplexer_1_out), .sel(reg_in_en));
  D_Flip_Flop d_ff_1 (.D(multiplexer_1_out), .clk(reg_clk), .Q(reg_int_out[7]));  // open: Qn, preset, reset
  assign reg_out[7] = reg_out_en ? reg_int_out[7] : 1'bz;  // Controlled_Buffer controlled_buffer_1
  Multiplexer multiplexer_2 (.in0(reg_int_out[6]), .in1(reg_in[6]), .out(multiplexer_2_out), .sel(reg_in_en));
  D_Flip_Flop d_ff_2 (.D(multiplexer_2_out), .clk(reg_clk), .Q(reg_int_out[6]));  // open: Qn, preset, reset
  assign reg_out[6] = reg_out_en ? reg_int_out[6] : 1'bz;  // Controlled_Buffer controlled_buffer_2
  Multiplexer multiplexer_3 (.in0(reg_int_out[5]), .in1(reg_in[5]), .out(multiplexer_3_out), .sel(reg_in_en));
  D_Flip_Flop d_ff_3 (.D(multiplexer_3_out), .clk(reg_clk), .Q(reg_int_out[5]));  // open: Qn, preset, reset
  assign reg_out[5] = reg_out_en ? reg_int_out[5] : 1'bz;  // Controlled_Buffer controlled_buffer_3
  D_Flip_Flop d_ff_4 (.D(multiplexer_4_out), .clk(reg_clk), .Q(reg_int_out[4]));  // open: Qn, preset, reset
  assign reg_out[4] = reg_out_en ? reg_int_out[4] : 1'bz;  // Controlled_Buffer controlled_buffer_4
  Multiplexer multiplexer_4 (.in0(reg_int_out[4]), .in1(reg_in[4]), .out(multiplexer_4_out), .sel(reg_in_en));
  Multiplexer multiplexer_5 (.in0(reg_int_out[3]), .in1(reg_in[3]), .out(multiplexer_5_out), .sel(reg_in_en));
  D_Flip_Flop d_ff_5 (.D(multiplexer_5_out), .clk(reg_clk), .Q(reg_int_out[3]));  // open: Qn, preset, reset
  assign reg_out[3] = reg_out_en ? reg_int_out[3] : 1'bz;  // Controlled_Buffer controlled_buffer_5
  Multiplexer multiplexer_6 (.in0(reg_int_out[2]), .in1(reg_in[2]), .out(multiplexer_6_out), .sel(reg_in_en));
  D_Flip_Flop d_ff_6 (.D(multiplexer_6_out), .clk(reg_clk), .Q(reg_int_out[2]));  // open: Qn, preset, reset
  assign reg_out[2] = reg_out_en ? reg_int_out[2] : 1'bz;  // Controlled_Buffer controlled_buffer_6
  Multiplexer multiplexer_7 (.in0(reg_int_out[1]), .in1(reg_in[1]), .out(multiplexer_7_out), .sel(reg_in_en));
  D_Flip_Flop d_ff_7 (.D(multiplexer_7_out), .clk(reg_clk), .Q(reg_int_out[1]));  // open: Qn, preset, reset
  assign reg_out[1] = reg_out_en ? reg_int_out[1] : 1'bz;  // Controlled_Buffer controlled_buffer_7
  Multiplexer multiplexer_8 (.in0(reg_int_out[0]), .in1(reg_in[0]), .out(multiplexer_8_out), .sel(reg_in_en));
  D_Flip_Flop d_ff_8 (.D(multiplexer_8_out), .clk(reg_clk), .Q(reg_int_out[0]));  // open: Qn, preset, reset
  assign reg_out[0] = reg_out_en ? reg_int_out[0] : 1'bz;  // Controlled_Buffer controlled_buffer_8
endmodule

module alu (
  input  [7:0] alu_in_1,
  input  alu_out_en,
  input  alu_sub,
  input  [7:0] alu_in_2,
  output [7:0] alu_out,
  output alu_carry_out
);

  wire adder_2_cout, adder_3_cout, adder_4_cout, adder_5_cout, adder_6_cout, adder_7_cout, adder_8_cout,
       xor_1_out, xor_2_out, xor_3_out, xor_4_out, xor_5_out, xor_6_out, xor_7_out, xor_8_out;
  wire [7:0] adder_8_out;

  Adder #(.width(1)) adder_1 (
    .a(alu_in_1[7]), .b(xor_1_out), .out(adder_8_out[7]), .cin(adder_2_cout), .cout(alu_carry_out));
  xor xor_1 (xor_1_out, alu_in_2[7], alu_sub);
  Adder #(.width(1)) adder_2 (
    .a(alu_in_1[6]), .b(xor_2_out), .out(adder_8_out[6]), .cin(adder_3_cout), .cout(adder_2_cout));
  xor xor_2 (xor_2_out, alu_in_2[6], alu_sub);
  Adder #(.width(1)) adder_3 (
    .a(alu_in_1[5]), .b(xor_3_out), .out(adder_8_out[5]), .cin(adder_4_cout), .cout(adder_3_cout));
  xor xor_3 (xor_3_out, alu_in_2[5], alu_sub);
  Adder #(.width(1)) adder_4 (
    .a(alu_in_1[4]), .b(xor_4_out), .out(adder_8_out[4]), .cin(adder_5_cout), .cout(adder_4_cout));
  Adder #(.width(1)) adder_5 (
    .a(alu_in_1[3]), .b(xor_5_out), .out(adder_8_out[3]), .cin(adder_6_cout), .cout(adder_5_cout));
  xor xor_4 (xor_4_out, alu_in_2[4], alu_sub);
  Adder #(.width(1)) adder_6 (
    .a(alu_in_1[2]), .b(xor_6_out), .out(adder_8_out[2]), .cin(adder_7_cout), .cout(adder_6_cout));
  xor xor_5 (xor_5_out, alu_in_2[3], alu_sub);
  Adder #(.width(1)) adder_7 (
    .a(alu_in_1[1]), .b(xor_7_out), .out(adder_8_out[1]), .cin(adder_8_cout), .cout(adder_7_cout));
  xor xor_6 (xor_6_out, alu_in_2[2], alu_sub);
  Adder #(.width(1)) adder_8 (.a(alu_in_1[0]), .b(xor_8_out), .out(adder_8_out[0]), .cin(alu_sub), .cout(adder_8_cout));
  xor xor_7 (xor_7_out, alu_in_2[1], alu_sub);
  xor xor_8 (xor_8_out, alu_in_2[0], alu_sub);
  assign alu_out = alu_out_en ? adder_8_out : 8'bz;  // Controlled_Buffer controlled_buffer_1
endmodule

module dec_4x16 (
  input  [3:0] dec_sel,
  output [15:0] dec_out
);

  wire not_1_out, not_2_out, not_3_out, not_4_out;

  not not_1 (not_1_out, dec_sel[3]);
  not not_2 (not_2_out, dec_sel[2]);
  not not_3 (not_3_out, dec_sel[1]);
  not not_4 (not_4_out, dec_sel[0]);
  and and_1 (dec_out[0], not_4_out, not_3_out, not_2_out, not_1_out);
  and and_2 (dec_out[1], dec_sel[0], not_3_out, not_2_out, not_1_out);
  and and_3 (dec_out[2], not_4_out, dec_sel[1], not_2_out, not_1_out);
  and and_4 (dec_out[3], dec_sel[0], dec_sel[1], not_2_out, not_1_out);
  and and_5 (dec_out[4], not_4_out, not_3_out, dec_sel[2], not_1_out);
  and and_6 (dec_out[5], dec_sel[0], not_3_out, dec_sel[2], not_1_out);
  and and_7 (dec_out[6], not_4_out, dec_sel[1], dec_sel[2], not_1_out);
  and and_8 (dec_out[7], dec_sel[0], dec_sel[1], dec_sel[2], not_1_out);
  and and_9 (dec_out[8], not_4_out, not_3_out, not_2_out, dec_sel[3]);
  and and_10 (dec_out[9], dec_sel[0], not_3_out, not_2_out, dec_sel[3]);
  and and_11 (dec_out[10], not_4_out, dec_sel[1], not_2_out, dec_sel[3]);
  and and_12 (dec_out[11], dec_sel[0], dec_sel[1], not_2_out, dec_sel[3]);
  and and_13 (dec_out[12], not_4_out, not_3_out, dec_sel[2], dec_sel[3]);
  and and_14 (dec_out[13], dec_sel[0], not_3_out, dec_sel[2], dec_sel[3]);
  and and_15 (dec_out[14], not_4_out, dec_sel[1], dec_sel[2], dec_sel[3]);
  and and_16 (dec_out[15], dec_sel[0], dec_sel[1], dec_sel[2], dec_sel[3]);
endmodule

module sram_cell (
  input  [7:0] data_in,
  input  wr_en,
  input  clk,
  input  cs,
  input  rd_en,
  output [7:0] memory_content,
  output [7:0] data_out
);

  wire and_1_out, and_2_out;

  and and_1 (and_1_out, wr_en, cs);
  and and_2 (and_2_out, cs, rd_en);
  reg_gp reg_gp_1 (
    .reg_in(data_in), .reg_in_en(and_1_out), .reg_clk(clk), .reg_out_en(and_2_out),
    .reg_int_out(memory_content), .reg_out(data_out));
endmodule

module prog_counter (
  input  pc_en,
  input  clk,
  input  pc_reset,
  input  pc_out_en,
  output [3:0] pc_value,
  output [3:0] pc_output
);

  wire j_k_ff_2_qn, j_k_ff_3_qn, j_k_ff_4_qn;

  J_K_Flip_Flop j_k_ff_1 (
    .J(pc_en), .K(pc_en), .clk(j_k_ff_2_qn), .Q(pc_value[3]), .reset(pc_reset));  // open: Qn, preset
  J_K_Flip_Flop j_k_ff_2 (
    .J(pc_en), .K(pc_en), .clk(j_k_ff_3_qn), .Q(pc_value[2]), .Qn(j_k_ff_2_qn), .reset(pc_reset));  // open: preset
  J_K_Flip_Flop j_k_ff_3 (
    .J(pc_en), .K(pc_en), .clk(j_k_ff_4_qn), .Q(pc_value[1]), .Qn(j_k_ff_3_qn), .reset(pc_reset));  // open: preset
  J_K_Flip_Flop j_k_ff_4 (
    .J(pc_en), .K(pc_en), .clk(clk), .Q(pc_value[0]), .Qn(j_k_ff_4_qn), .reset(pc_reset));  // open: preset
  assign pc_output = pc_out_en ? pc_value : 4'bz;  // Controlled_Buffer controlled_buffer_1

  // Notes on the sheet:
  //   Clock
  //   Reset
  //   Output Control
  //   Count Control
  //   Counter Output
endmodule

module ram_cir (
  input  sram_rd,
  input  sram_wr,
  input  [7:0] sram_d_in,
  input  [7:0] mar_d_in,
  input  mar_in_en,
  input  sram_clk,
  output [7:0] sram_d_out,
  output [7:0] out_8,
  output [7:0] out_9,
  output [7:0] out_10,
  output [7:0] out_11,
  output [7:0] out_12,
  output [7:0] out_13,
  output [7:0] out_14,
  output [7:0] out_15,
  output [7:0] out_16,
  output [7:0] out_17,
  output [7:0] out_18,
  output [7:0] out_19,
  output [7:0] out_20,
  output [7:0] out_21,
  output [7:0] out_22,
  output [7:0] out_23
);

  wire [7:0] reg_gp_1_reg_int_out, sram_cell_1_data_out;
  wire [15:0] dec_4x16_1_dec_out;

  reg_gp reg_gp_1 (
    .reg_in(mar_d_in), .reg_in_en(mar_in_en), .reg_clk(sram_clk), .reg_int_out(reg_gp_1_reg_int_out));  // open: reg_out_en, reg_out
  dec_4x16 dec_4x16_1 (.dec_sel(reg_gp_1_reg_int_out[3:0]), .dec_out(dec_4x16_1_dec_out));
  sram_cell sram_cell_1 (
    .data_in(sram_cell_1_data_out), .wr_en(sram_wr), .clk(sram_clk), .cs(dec_4x16_1_dec_out[0]),
    .rd_en(sram_rd), .memory_content(out_8), .data_out(sram_cell_1_data_out));
  sram_cell sram_cell_2 (
    .data_in(sram_cell_1_data_out), .wr_en(sram_wr), .clk(sram_clk), .cs(dec_4x16_1_dec_out[1]),
    .rd_en(sram_rd), .memory_content(out_9), .data_out(sram_cell_1_data_out));
  sram_cell sram_cell_3 (
    .data_in(sram_cell_1_data_out), .wr_en(sram_wr), .clk(sram_clk), .cs(dec_4x16_1_dec_out[2]),
    .rd_en(sram_rd), .memory_content(out_10), .data_out(sram_cell_1_data_out));
  sram_cell sram_cell_4 (
    .data_in(sram_cell_1_data_out), .wr_en(sram_wr), .clk(sram_clk), .cs(dec_4x16_1_dec_out[3]),
    .rd_en(sram_rd), .memory_content(out_11), .data_out(sram_cell_1_data_out));
  sram_cell sram_cell_5 (
    .data_in(sram_cell_1_data_out), .wr_en(sram_wr), .clk(sram_clk), .cs(dec_4x16_1_dec_out[4]),
    .rd_en(sram_rd), .memory_content(out_12), .data_out(sram_cell_1_data_out));
  sram_cell sram_cell_6 (
    .data_in(sram_cell_1_data_out), .wr_en(sram_wr), .clk(sram_clk), .cs(dec_4x16_1_dec_out[5]),
    .rd_en(sram_rd), .memory_content(out_13), .data_out(sram_cell_1_data_out));
  sram_cell sram_cell_7 (
    .data_in(sram_cell_1_data_out), .wr_en(sram_wr), .clk(sram_clk), .cs(dec_4x16_1_dec_out[6]),
    .rd_en(sram_rd), .memory_content(out_14), .data_out(sram_cell_1_data_out));
  sram_cell sram_cell_8 (
    .data_in(sram_cell_1_data_out), .wr_en(sram_wr), .clk(sram_clk), .cs(dec_4x16_1_dec_out[7]),
    .rd_en(sram_rd), .memory_content(out_15), .data_out(sram_cell_1_data_out));
  sram_cell sram_cell_9 (
    .data_in(sram_cell_1_data_out), .wr_en(sram_wr), .clk(sram_clk), .cs(dec_4x16_1_dec_out[8]),
    .rd_en(sram_rd), .memory_content(out_16), .data_out(sram_cell_1_data_out));
  sram_cell sram_cell_10 (
    .data_in(sram_cell_1_data_out), .wr_en(sram_wr), .clk(sram_clk), .cs(dec_4x16_1_dec_out[9]),
    .rd_en(sram_rd), .memory_content(out_17), .data_out(sram_cell_1_data_out));
  sram_cell sram_cell_11 (
    .data_in(sram_cell_1_data_out), .wr_en(sram_wr), .clk(sram_clk), .cs(dec_4x16_1_dec_out[10]),
    .rd_en(sram_rd), .memory_content(out_18), .data_out(sram_cell_1_data_out));
  sram_cell sram_cell_12 (
    .data_in(sram_cell_1_data_out), .wr_en(sram_wr), .clk(sram_clk), .cs(dec_4x16_1_dec_out[11]),
    .rd_en(sram_rd), .memory_content(out_19), .data_out(sram_cell_1_data_out));
  sram_cell sram_cell_13 (
    .data_in(sram_cell_1_data_out), .wr_en(sram_wr), .clk(sram_clk), .cs(dec_4x16_1_dec_out[12]),
    .rd_en(sram_rd), .memory_content(out_20), .data_out(sram_cell_1_data_out));
  sram_cell sram_cell_14 (
    .data_in(sram_cell_1_data_out), .wr_en(sram_wr), .clk(sram_clk), .cs(dec_4x16_1_dec_out[13]),
    .rd_en(sram_rd), .memory_content(out_21), .data_out(sram_cell_1_data_out));
  sram_cell sram_cell_15 (
    .data_in(sram_cell_1_data_out), .wr_en(sram_wr), .clk(sram_clk), .cs(dec_4x16_1_dec_out[14]),
    .rd_en(sram_rd), .memory_content(out_22), .data_out(sram_cell_1_data_out));
  sram_cell sram_cell_16 (
    .data_in(sram_cell_1_data_out), .wr_en(sram_wr), .clk(sram_clk), .cs(dec_4x16_1_dec_out[15]),
    .rd_en(sram_rd), .memory_content(out_23), .data_out(sram_cell_1_data_out));
  assign sram_cell_1_data_out = sram_wr ? sram_d_in : 8'bz;  // Controlled_Buffer controlled_buffer_1
  assign sram_d_out = sram_rd ? sram_cell_1_data_out : 8'bz;  // Controlled_Buffer controlled_buffer_2
endmodule

module ins_reg (
  input  [7:0] ins_reg_in,
  input  ins_reg_in_en,
  input  clk,
  input  ins_reg_out_en,
  output [3:0] add_outs,
  output [3:0] ins_out
);

  wire [3:0] reg_gp_1_reg_int_out;

  reg_gp reg_gp_1 (
    .reg_in(ins_reg_in), .reg_in_en(ins_reg_in_en), .reg_clk(clk),
    .reg_int_out({ins_out, reg_gp_1_reg_int_out}));  // open: reg_out_en, reg_out
  assign add_outs = ins_reg_out_en ? reg_gp_1_reg_int_out : 4'bz;  // Controlled_Buffer controlled_buffer_1
endmodule

module T_states (
  input  T6,
  input  T5,
  input  T4,
  input  T3,
  input  T2,
  input  T1,
  output O1,
  output O2,
  output O3
);

  or or_1 (O1, T5, T3, T1);
  or or_2 (O2, T6, T3, T2);
  or or_3 (O3, T6, T5, T4);
endmodule

module cont_seqqq (
  input  clk,
  input  CLR,
  input  [3:0] dec_sel,
  input  en,
  output T6,
  output T5,
  output T4,
  output T3,
  output T2,
  output T1,
  output ins_reg_out_en,
  output a_in,
  output b_in,
  output add_out,
  output sub_out,
  output sram_wr,
  output alu_out_en,
  output sft_dir,
  output rot_dir,
  output pc_en,
  output mar_in_en,
  output pc_out,
  output sram_rd,
  output ins_reg_in_en,
  output new_reg_in,
  output new_reg_out,
  output a_out,
  output sft_am,
  output rot_am,
  output sft_in,
  output rot_in,
  output sft_out_en,
  output rot_out_en,
  output sft_out,
  output rot_out,
  output sft_reg_in_en,
  output rot_reg_in_en,
  output reg_a_out_en,
  output HLT
);

  wire add_out_2, and_1_out, and_2_out, and_3_out, and_4_out, and_5_out, and_6_out, and_7_out, and_8_out,
       and_9_out, and_10_out, and_11_out, and_12_out, and_13_out, and_14_out, and_15_out, and_16_out,
       halt_out, j_k_ff_1_q, j_k_ff_2_qn, j_k_ff_3_qn, j_k_ff_4_qn, j_k_ff_5_qn, j_k_ff_6_qn, load_out,
       nand_1_out, nand_2_out, nand_3_out, nand_4_out, nand_5_out, nand_6_out, nand_7_out, nand_8_out,
       nand_9_out, nand_10_out, nand_11_out, nand_12_out, nand_13_out, nand_14_out, nand_15_out, nand_16_out,
       nand_17_out, nand_18_out, nand_19_out, nand_20_out, nand_21_out, nand_22_out, nand_23_out,
       nand_24_out, nand_25_out, nand_26_out, nand_27_out, nand_28_out, nand_29_out, nand_30_out,
       nand_31_out, nand_32_out, nand_33_out, nand_34_out, nand_35_out, nand_36_out, nand_37_out,
       nand_38_out, nand_39_out, nand_40_out, nand_41_out, nand_42_out, nand_43_out, nand_44_out,
       nand_45_out, nand_46_out, nand_47_out, nand_48_out, nand_49_out, nand_50_out, nand_51_out,
       nand_52_out, nand_53_out, nand_54_out, nand_55_out, nand_56_out, nand_57_out, nand_58_out,
       nand_59_out, nand_60_out, nand_61_out, nand_62_out, nand_63_out, not_1_out, not_2_out, not_3_out,
       not_4_out, not_6_out, not_7_out, or_1_out, or_2_out, or_3_out, or_4_out, or_5_out, or_6_out, or_7_out,
       or_8_out, or_9_out, or_10_out, rotl_out, rotr_out, shl_out, shr_out, str_out, sub_out_2;

  not not_1 (not_1_out, dec_sel[3]);
  not not_2 (not_2_out, dec_sel[2]);
  not not_3 (not_3_out, dec_sel[1]);
  not not_4 (not_4_out, dec_sel[0]);
  and load (load_out, dec_sel[0], not_3_out, not_2_out, not_1_out);
  and add (add_out_2, not_4_out, dec_sel[1], not_2_out, not_1_out);
  and sub (sub_out_2, dec_sel[0], dec_sel[1], not_2_out, not_1_out);
  and str (str_out, not_4_out, not_3_out, dec_sel[2], not_1_out);
  and shl (shl_out, dec_sel[0], not_3_out, dec_sel[2], not_1_out);
  and shr (shr_out, not_4_out, dec_sel[1], dec_sel[2], not_1_out);
  and rotl (rotl_out, dec_sel[0], dec_sel[1], dec_sel[2], not_1_out);
  and rotr (rotr_out, not_4_out, not_3_out, not_2_out, dec_sel[3]);
  and halt (halt_out, dec_sel[0], dec_sel[1], dec_sel[2], dec_sel[3]);
  not not_5 (HLT, halt_out);
  not not_6 (not_6_out, T1);
  nand nand_1 (nand_1_out, T4, load_out);
  J_K_Flip_Flop j_k_ff_1 (.J(j_k_ff_6_qn), .K(T6), .clk(clk), .Q(j_k_ff_1_q), .Qn(T1), .reset(CLR));  // open: preset
  nand nand_2 (nand_2_out, T4, add_out_2);
  nand nand_3 (nand_3_out, T4, sub_out_2);
  J_K_Flip_Flop j_k_ff_2 (.J(T1), .K(j_k_ff_1_q), .clk(clk), .Q(T2), .Qn(j_k_ff_2_qn), .reset(CLR));  // open: preset
  nand nand_4 (nand_4_out, T4, str_out);
  nand nand_5 (nand_5_out, T4, shl_out);
  nand nand_6 (nand_6_out, not_6_out, nand_1_out, nand_2_out, nand_3_out, nand_4_out, nand_5_out, nand_7_out, nand_8_out, nand_9_out);
  assign mar_in_en = en ? nand_6_out : 1'bz;  // Controlled_Buffer controlled_buffer_1
  nand nand_7 (nand_7_out, T4, shr_out);
  J_K_Flip_Flop j_k_ff_3 (.J(T2), .K(j_k_ff_2_qn), .clk(clk), .Q(T3), .Qn(j_k_ff_3_qn), .reset(CLR));  // open: preset
  nand nand_8 (nand_8_out, T4, rotl_out);
  nand nand_9 (nand_9_out, T4, rotr_out);
  J_K_Flip_Flop j_k_ff_4 (.J(T3), .K(j_k_ff_3_qn), .clk(clk), .Q(T4), .Qn(j_k_ff_4_qn), .reset(CLR));  // open: preset
  assign pc_out = en ? T1 : 1'bz;  // Controlled_Buffer controlled_buffer_2
  J_K_Flip_Flop j_k_ff_5 (.J(T4), .K(j_k_ff_4_qn), .clk(clk), .Q(T5), .Qn(j_k_ff_5_qn), .reset(CLR));  // open: preset
  not not_7 (not_7_out, T2);
  nand nand_10 (nand_10_out, T5, load_out);
  J_K_Flip_Flop j_k_ff_6 (.J(T5), .K(j_k_ff_5_qn), .clk(clk), .Q(T6), .Qn(j_k_ff_6_qn), .reset(CLR));  // open: preset
  nand nand_11 (nand_11_out, T5, add_out_2);
  nand nand_12 (nand_12_out, T5, sub_out_2);
  nand nand_13 (nand_13_out, T5, str_out);
  nand nand_14 (nand_14_out, not_7_out, nand_10_out, nand_11_out, nand_12_out, nand_13_out, nand_15_out, nand_16_out, nand_17_out, nand_18_out);
  assign sram_rd = en ? nand_14_out : 1'bz;  // Controlled_Buffer controlled_buffer_3
  nand nand_15 (nand_15_out, T5, shl_out);
  nand nand_16 (nand_16_out, T5, shr_out);
  nand nand_17 (nand_17_out, T5, rotl_out);
  nand nand_18 (nand_18_out, T5, rotr_out);
  assign ins_reg_in_en = en ? T2 : 1'bz;  // Controlled_Buffer controlled_buffer_4
  nand nand_19 (nand_19_out, T4, load_out);
  nand nand_20 (nand_20_out, T4, add_out_2);
  nand nand_21 (nand_21_out, T4, sub_out_2);
  nand nand_22 (nand_22_out, T4, str_out);
  nand nand_23 (nand_23_out, T4, shl_out);
  nand nand_24 (nand_24_out, nand_19_out, nand_20_out, nand_21_out, nand_22_out, nand_25_out, nand_26_out, nand_27_out);
  assign ins_reg_out_en = en ? nand_24_out : 1'bz;  // Controlled_Buffer controlled_buffer_5
  nand nand_25 (nand_25_out, T4, shr_out);
  nand nand_26 (nand_26_out, T4, rotl_out);
  nand nand_27 (nand_27_out, T4, rotr_out);
  and and_1 (and_1_out, T5, load_out);
  and and_2 (and_2_out, T6, or_2_out);
  or or_1 (or_1_out, and_1_out, and_2_out);
  assign a_in = en ? or_1_out : 1'bz;  // Controlled_Buffer controlled_buffer_6
  or or_2 (or_2_out, add_out_2, sub_out_2, shl_out, shr_out, rotl_out, rotr_out);
  or or_3 (or_3_out, add_out_2, sub_out_2);
  and and_3 (and_3_out, T5, or_3_out);
  assign b_in = en ? and_3_out : 1'bz;  // Controlled_Buffer controlled_buffer_7
  and and_4 (and_4_out, T6, add_out_2);
  assign add_out = en ? and_4_out : 1'bz;  // Controlled_Buffer controlled_buffer_8
  and and_5 (and_5_out, T6, sub_out_2);
  assign sub_out = en ? and_5_out : 1'bz;  // Controlled_Buffer controlled_buffer_9
  nand nand_28 (nand_28_out, T2, shl_out);
  nand nand_29 (nand_29_out, T2, shr_out);
  nand nand_30 (nand_30_out, T2, rotl_out);
  nand nand_31 (nand_31_out, nand_28_out, nand_29_out, nand_30_out, nand_32_out);
  assign new_reg_in = en ? nand_31_out : 1'bz;  // Controlled_Buffer controlled_buffer_10
  nand nand_32 (nand_32_out, T2, rotr_out);
  nand nand_33 (nand_33_out, T5, shl_out);
  nand nand_34 (nand_34_out, T5, shr_out);
  nand nand_35 (nand_35_out, nand_33_out, nand_34_out, nand_36_out, nand_37_out);
  assign new_reg_out = en ? nand_35_out : 1'bz;  // Controlled_Buffer controlled_buffer_11
  nand nand_36 (nand_36_out, T5, rotl_out);
  nand nand_37 (nand_37_out, T5, rotr_out);
  nand nand_38 (nand_38_out, T5, shl_out);
  nand nand_39 (nand_39_out, T5, shr_out);
  nand nand_40 (nand_40_out, T5, rotl_out);
  nand nand_41 (nand_41_out, T5, rotr_out);
  nand nand_42 (nand_42_out, nand_38_out, nand_39_out, nand_40_out, nand_41_out);
  assign a_out = en ? nand_42_out : 1'bz;  // Controlled_Buffer controlled_buffer_12
  and and_6 (and_6_out, T6, str_out);
  assign sram_wr = en ? and_6_out : 1'bz;  // Controlled_Buffer controlled_buffer_13
  and and_7 (and_7_out, T6, or_4_out);
  assign alu_out_en = en ? and_7_out : 1'bz;  // Controlled_Buffer controlled_buffer_14
  or or_4 (or_4_out, add_out_2, sub_out_2);
  nand nand_43 (nand_43_out, T5, shl_out);
  nand nand_44 (nand_44_out, T5, shr_out);
  nand nand_45 (nand_45_out, nand_43_out, nand_44_out);
  assign sft_am = en ? nand_45_out : 1'bz;  // Controlled_Buffer controlled_buffer_15
  nand nand_46 (nand_46_out, T5, rotl_out);
  nand nand_47 (nand_47_out, T5, rotr_out);
  nand nand_48 (nand_48_out, nand_46_out, nand_47_out);
  assign rot_am = en ? nand_48_out : 1'bz;  // Controlled_Buffer controlled_buffer_16
  and and_8 (and_8_out, T5, shl_out);
  assign sft_dir = en ? and_8_out : 1'bz;  // Controlled_Buffer controlled_buffer_17
  and and_9 (and_9_out, T5, rotl_out);
  assign rot_dir = en ? and_9_out : 1'bz;  // Controlled_Buffer controlled_buffer_18
  nand nand_49 (nand_49_out, T5, shl_out);
  nand nand_50 (nand_50_out, T5, shr_out);
  nand nand_51 (nand_51_out, nand_49_out, nand_50_out);
  assign sft_in = en ? nand_51_out : 1'bz;  // Controlled_Buffer controlled_buffer_19
  nand nand_52 (nand_52_out, T5, rotl_out);
  nand nand_53 (nand_53_out, T5, rotr_out);
  nand nand_54 (nand_54_out, nand_52_out, nand_53_out);
  assign rot_in = en ? nand_54_out : 1'bz;  // Controlled_Buffer controlled_buffer_20
  and and_10 (and_10_out, str_out, T6);
  assign reg_a_out_en = en ? and_10_out : 1'bz;  // Controlled_Buffer controlled_buffer_21
  or or_5 (or_5_out, shl_out, shr_out);
  and and_11 (and_11_out, T6, or_5_out);
  assign sft_out_en = en ? and_11_out : 1'bz;  // Controlled_Buffer controlled_buffer_22
  or or_6 (or_6_out, rotl_out, rotr_out);
  and and_12 (and_12_out, T6, or_6_out);
  assign rot_out_en = en ? and_12_out : 1'bz;  // Controlled_Buffer controlled_buffer_23
  nand nand_55 (nand_55_out, T3, load_out);
  nand nand_56 (nand_56_out, T3, add_out_2);
  nand nand_57 (nand_57_out, T3, sub_out_2);
  nand nand_58 (nand_58_out, T3, str_out);
  nand nand_59 (nand_59_out, T3, shl_out);
  nand nand_60 (nand_60_out, nand_55_out, nand_56_out, nand_57_out, nand_58_out, nand_61_out, nand_62_out, nand_63_out);
  assign pc_en = en ? nand_60_out : 1'bz;  // Controlled_Buffer controlled_buffer_24
  nand nand_61 (nand_61_out, T3, shr_out);
  nand nand_62 (nand_62_out, T3, rotl_out);
  nand nand_63 (nand_63_out, T3, rotr_out);
  and and_13 (and_13_out, T6, or_7_out);
  assign sft_out = en ? and_13_out : 1'bz;  // Controlled_Buffer controlled_buffer_25
  or or_7 (or_7_out, shl_out, shr_out);
  and and_14 (and_14_out, T6, or_8_out);
  assign rot_out = en ? and_14_out : 1'bz;  // Controlled_Buffer controlled_buffer_26
  or or_8 (or_8_out, rotl_out, rotr_out);
  or or_9 (or_9_out, shl_out, shr_out);
  and and_15 (and_15_out, T5, or_9_out);
  assign sft_reg_in_en = en ? and_15_out : 1'bz;  // Controlled_Buffer controlled_buffer_27
  or or_10 (or_10_out, rotl_out, rotr_out);
  and and_16 (and_16_out, T5, or_10_out);
  assign rot_reg_in_en = en ? and_16_out : 1'bz;  // Controlled_Buffer controlled_buffer_28

  // Notes on the sheet:
  //   Decoder
  //   Ring Counter
  //   States
endmodule

module data_loader (
  input  clk,
  input  reset,
  input  enable,
  input  debug,
  output [3:0] address,
  output [3:0] out_6,
  output [7:0] data,
  output t1,
  output t2,
  output mar_in_en,
  output sram_wr
);

  wire address_en, and_1_out, and_2_out, and_3_out, and_6_out, and_7_out, and_8_out, and_9_out, and_10_out,
       controlled_buffer_1_out, controlled_buffer_3_out, d_ff_1_q, data_en, fdl_reg_en, fdl_reg_out_en,
       not_1_out;
  wire [3:0] new_reg_1_reg_out;
  wire [7:0] rom_1_data;

  assign controlled_buffer_1_out = address_en ? clk : 1'bz;  // Controlled_Buffer controlled_buffer_1
  and and_1 (and_1_out, debug, t1);
  assign address_en = enable ? and_1_out : 1'bz;  // Controlled_Buffer controlled_buffer_2
  J_K_Flip_Flop j_k_ff_1 (
    .J(enable), .K(enable), .clk(controlled_buffer_1_out), .Q(address[0]), .reset(reset));  // open: Qn, preset
  assign controlled_buffer_3_out = debug ? not_1_out : 1'bz;  // Controlled_Buffer controlled_buffer_3
  J_K_Flip_Flop j_k_ff_2 (
    .J(address[0]), .K(address[0]), .clk(controlled_buffer_1_out), .Q(address[1]), .reset(reset));  // open: Qn, preset
  D_Flip_Flop d_ff_1 (.D(controlled_buffer_3_out), .clk(clk), .Q(d_ff_1_q), .reset(reset));  // open: Qn, preset
  and and_2 (and_2_out, debug, t1);
  assign mar_in_en = enable ? and_2_out : 1'bz;  // Controlled_Buffer controlled_buffer_4
  J_K_Flip_Flop j_k_ff_3 (
    .J(and_3_out), .K(and_3_out), .clk(controlled_buffer_1_out), .Q(address[2]), .reset(reset));  // open: Qn, preset
  and and_3 (and_3_out, address[0], address[1]);
  not not_1 (not_1_out, d_ff_1_q);
  J_K_Flip_Flop j_k_ff_4 (
    .J(and_7_out), .K(and_7_out), .clk(controlled_buffer_1_out), .Q(address[3]), .reset(reset));  // open: Qn, preset
  and and_4 (t1, debug, not_1_out);
  and and_5 (t2, d_ff_1_q, debug);
  and and_6 (and_6_out, debug, t2);
  assign data_en = enable ? and_6_out : 1'bz;  // Controlled_Buffer controlled_buffer_5
  and and_7 (and_7_out, and_3_out, address[2]);
  and and_8 (and_8_out, debug, t2);
  assign sram_wr = enable ? and_8_out : 1'bz;  // Controlled_Buffer controlled_buffer_6
  and and_9 (and_9_out, debug, t1);
  assign fdl_reg_en = enable ? and_9_out : 1'bz;  // Controlled_Buffer controlled_buffer_7
  and and_10 (and_10_out, debug, t2);
  assign fdl_reg_out_en = enable ? and_10_out : 1'bz;  // Controlled_Buffer controlled_buffer_8
  new_reg new_reg_1 (
    .reg_in(address), .reg_in_en(fdl_reg_en), .reg_clk(controlled_buffer_1_out), .reg_out_en(fdl_reg_out_en),
    .reg_int_out(out_6), .reg_out(new_reg_1_reg_out));
  ROM #(.addrWidth(4)) rom_1 (.addr(new_reg_1_reg_out), .data(rom_1_data));
  assign data = data_en ? rom_1_data : 8'bz;  // Controlled_Buffer controlled_buffer_9

  // Notes on the sheet:
  //   Control Sequencer for Data Loader
  //   Address register
  //   contents of rom_1 (hex, n*v repeats v):
  //   1c 2d 4e 84 73 62 52 5*0 ae af
  //   ROM
endmodule

module pro_prac_2 (
  input  in_1,
  input  in_2,
  input  in_3,
  input  in_4,
  input  in_5,
  input  in_6,
  output out_7,
  output out_8,
  output out_9,
  output out_10,
  output out_11,
  output [3:0] out_12,
  output [7:0] out_13,
  output [7:0] out_14,
  output out_15,
  output out_16,
  output [7:0] out_17,
  output out_18,
  output out_19,
  output out_20,
  output out_21,
  output [7:0] out_22,
  output [7:0] out_23,
  output [7:0] out_24,
  output [7:0] out_25,
  output out_26,
  output [7:0] out_27,
  output [7:0] out_28,
  output [7:0] out_29,
  output [7:0] out_30,
  output out_31,
  output [7:0] out_32,
  output [7:0] out_33,
  output [7:0] out_34,
  output out_35,
  output [7:0] out_36,
  output [3:0] out_37,
  output [7:0] out_38,
  output [3:0] out_39,
  output [7:0] out_40,
  output out_41,
  output [7:0] out_42,
  output [7:0] out_43,
  output [7:0] out_44,
  output out_45,
  output [3:0] out_46,
  output out_47,
  output out_48,
  output out_49,
  output out_50,
  output out_51,
  output [3:0] out_52,
  output [7:0] out_53,
  output out_54,
  output out_55,
  output out_56,
  output out_57,
  output out_58,
  output out_59,
  output out_60
);

  wire a_in, a_out, alu_out, alu_out_en, alu_sub, and_1_out, and_2_out, b_in, cont_seqqq_1_hlt,
       cont_seqqq_1_t1, cont_seqqq_1_t2, cont_seqqq_1_t3, cont_seqqq_1_t4, cont_seqqq_1_t5, cont_seqqq_1_t6,
       controlled_buffer_3_out, data_loader_1_p6, ins_reg_in_en, ins_reg_out_en, mar_in_en, new_reg_in,
       new_reg_out, pc_en, pc_out, reg_a_out_en, rot_am, rot_dir, rot_in, rot_out, rot_out_en, rot_reg_in_en,
       sft_am, sft_dir, sft_in, sft_out, sft_out_en, sft_reg_in_en, sram_rd, sram_wr, t1, t2;
  wire [3:0] alu_2_1_alu_output, alu_2_1_alu_output_2, alu_2_1_rotate_output, alu_2_1_rotate_output_2,
       alu_2_1_shift_output, alu_2_1_shift_output_2, controlled_buffer_6_out, controlled_buffer_7_out,
       new_reg_1_reg_int_out, new_reg_1_reg_out, undriven;
  wire [7:0] controlled_buffer_4_out, controlled_buffer_5_out, multiplexer_1_out, reg_gp_1_reg_out;

  Multiplexer #(.width(8)) multiplexer_1 (.in0(out_17), .in1({undriven, out_52}), .out(multiplexer_1_out), .sel(in_5));
  Hex_Digit_Display hex_digit_display_1 (.value(out_12));  // open: dp
  prog_counter prog_counter_1 (
    .pc_en(pc_en), .clk(in_3), .pc_reset(in_4), .pc_out_en(pc_out), .pc_value(out_12), .pc_output(out_17[3:0]));
  Hex_Digit_Display hex_digit_display_2 (.value(out_17[7:4]));  // open: dp
  Hex_Digit_Display hex_digit_display_3 (.value(out_17[3:0]));  // open: dp
  ram_cir ram_cir_1 (
    .sram_rd(sram_rd), .sram_wr(sram_wr), .sram_d_in(out_17), .mar_d_in(multiplexer_1_out),
    .mar_in_en(mar_in_en), .sram_clk(in_3), .sram_d_out(out_17), .out_8(out_23), .out_9(out_24),
    .out_10(out_25), .out_11(out_27), .out_12(out_28), .out_13(out_29), .out_14(out_30), .out_15(out_32),
    .out_16(out_33), .out_17(out_34), .out_18(out_36), .out_19(out_38), .out_20(out_40), .out_21(out_42),
    .out_22(out_43), .out_23(out_44));
  Hex_Digit_Display hex_digit_display_4 (.value(out_52));  // open: dp
  // data_loader data_loader_1: pin names not known; wires that end beside it: in_3, in_4, in_1, in_5, out_52, data_loader_1_p6, t1, out_53, t2, mar_in_en, sram_wr
  Hex_Digit_Display hex_digit_display_5 (.value(out_17[7:4]));  // open: dp
  Hex_Digit_Display hex_digit_display_6 (.value(out_17[3:0]));  // open: dp
  Hex_Digit_Display hex_digit_display_7 (.value(out_53[7:4]));  // open: dp
  Hex_Digit_Display hex_digit_display_8 (.value(out_53[3:0]));  // open: dp
  assign out_17 = in_5 ? out_53 : 8'bz;  // Controlled_Buffer controlled_buffer_1
  and and_1 (and_1_out, in_3, cont_seqqq_1_hlt);
  assign out_17 = reg_a_out_en ? out_13 : 8'bz;  // Controlled_Buffer controlled_buffer_2
  assign controlled_buffer_3_out = in_2 ? and_1_out : 1'bz;  // Controlled_Buffer controlled_buffer_3
  Hex_Digit_Display hex_digit_display_9 (.value(out_13[7:4]));  // open: dp
  reg_gp reg_gp_1 (
    .reg_in(out_17), .reg_in_en(a_in), .reg_clk(in_3), .reg_out_en(a_out), .reg_int_out(out_13),
    .reg_out(reg_gp_1_reg_out));
  reg_gp reg_gp_2 (
    .reg_in(out_17), .reg_in_en(b_in), .reg_clk(in_3), .reg_out_en(in_6), .reg_int_out(out_22),
    .reg_out(reg_gp_1_reg_out));
  Hex_Digit_Display hex_digit_display_10 (.value(out_22[7:4]));  // open: dp
  ins_reg ins_reg_1 (
    .ins_reg_in(out_17), .ins_reg_in_en(ins_reg_in_en), .clk(in_3), .ins_reg_out_en(ins_reg_out_en),
    .add_outs(out_17[3:0]), .ins_out(out_39));
  Hex_Digit_Display hex_digit_display_11 (.value(out_13[3:0]));  // open: dp
  Hex_Digit_Display hex_digit_display_12 (.value(out_22[3:0]));  // open: dp
  Hex_Digit_Display hex_digit_display_13 (.value(out_39), .dp(out_39[0]));
  Hex_Digit_Display hex_digit_display_14 (.value(out_14[7:4]));  // open: dp
  Hex_Digit_Display hex_digit_display_15 (.value(out_14[3:0]));  // open: dp
  cont_seqqq cont_seqqq_1 (
    .clk(controlled_buffer_3_out), .CLR(in_4), .dec_sel(out_39), .en(in_2), .T6(cont_seqqq_1_t6),
    .T5(cont_seqqq_1_t5), .T4(cont_seqqq_1_t4), .T3(cont_seqqq_1_t3), .T2(cont_seqqq_1_t2),
    .T1(cont_seqqq_1_t1), .ins_reg_out_en(ins_reg_out_en), .a_in(a_in), .b_in(b_in), .add_out(alu_out),
    .sub_out(alu_sub), .sram_wr(sram_wr), .alu_out_en(alu_out_en), .sft_dir(sft_dir), .rot_dir(rot_dir),
    .pc_en(pc_en), .mar_in_en(mar_in_en), .pc_out(pc_out), .sram_rd(sram_rd), .ins_reg_in_en(ins_reg_in_en),
    .new_reg_in(new_reg_in), .new_reg_out(new_reg_out), .a_out(a_out), .sft_am(sft_am), .rot_am(rot_am),
    .sft_in(sft_in), .rot_in(rot_in), .sft_out_en(sft_out_en), .rot_out_en(rot_out_en), .sft_out(sft_out),
    .rot_out(rot_out), .sft_reg_in_en(sft_reg_in_en), .rot_reg_in_en(rot_reg_in_en),
    .reg_a_out_en(reg_a_out_en), .HLT(cont_seqqq_1_hlt));
  Hex_Digit_Display hex_digit_display_16 (.value(out_17[3:0]));  // open: dp
  LED led_1 (.in(and_2_out));
  and and_2 (and_2_out, in_1, in_5);
  assign controlled_buffer_4_out = sft_in ? out_13 : 8'bz;  // Controlled_Buffer controlled_buffer_4
  assign controlled_buffer_5_out = rot_in ? out_13 : 8'bz;  // Controlled_Buffer controlled_buffer_5
  new_reg new_reg_1 (
    .reg_in(out_17[3:0]), .reg_in_en(new_reg_in), .reg_clk(in_3), .reg_out_en(new_reg_out),
    .reg_int_out(new_reg_1_reg_int_out), .reg_out(new_reg_1_reg_out));
  Hex_Digit_Display hex_digit_display_17 (.value({1'b0, out_46[2:0]}));  // open: dp
  assign controlled_buffer_6_out = sft_am ? new_reg_1_reg_out : 4'bz;  // Controlled_Buffer controlled_buffer_6
  assign controlled_buffer_7_out = rot_am ? new_reg_1_reg_out : 4'bz;  // Controlled_Buffer controlled_buffer_7
  Hex_Digit_Display hex_digit_display_18 (.value(new_reg_1_reg_out));  // open: dp
  LED led_2 (.in(in_3));
  Hex_Digit_Display hex_digit_display_19 (.value(new_reg_1_reg_int_out));  // open: dp
  LED led_3 (.in(in_2));
  Hex_Digit_Display hex_digit_display_20 (.value(alu_2_1_alu_output_2));  // open: dp
  Hex_Digit_Display hex_digit_display_21 (.value(alu_2_1_alu_output));  // open: dp
  alu_2 alu_2_1 (
    .reg_a(out_13), .alu_out(alu_out), .alu_sub(alu_sub), .reg_b(out_22),
    .shift_in_data(controlled_buffer_4_out), .shift_direction(sft_dir), .sft_reg_in_en(sft_reg_in_en),
    .shift_amount(controlled_buffer_6_out), .sft_out(sft_out), .clk(in_3),
    .rotate_in_data(controlled_buffer_5_out), .rotate_direction(rot_dir), .rot_reg_in_en(rot_reg_in_en),
    .rotate_amount(controlled_buffer_7_out), .rot_out(rot_out),
    .alu_output({alu_2_1_alu_output_2, alu_2_1_alu_output}),
    .shift_output({alu_2_1_shift_output_2, alu_2_1_shift_output}),
    .rotate_output({alu_2_1_rotate_output_2, alu_2_1_rotate_output}));  // open: alu_carry_out
  T_states t_states_1 (
    .T6(cont_seqqq_1_t6), .T5(cont_seqqq_1_t5), .T4(cont_seqqq_1_t4), .T3(cont_seqqq_1_t3),
    .T2(cont_seqqq_1_t2), .T1(cont_seqqq_1_t1), .O1(out_46[0]), .O2(out_46[1]), .O3(out_46[2]));
  Hex_Digit_Display hex_digit_display_22 (.value(alu_2_1_shift_output_2));  // open: dp
  assign out_17 = alu_out_en ? {alu_2_1_alu_output_2, alu_2_1_alu_output} : 8'bz;  // Controlled_Buffer controlled_buffer_8
  assign out_17 = rot_out_en ? {alu_2_1_rotate_output_2, alu_2_1_rotate_output} : 8'bz;  // Controlled_Buffer controlled_buffer_9
  Hex_Digit_Display hex_digit_display_23 (.value(alu_2_1_shift_output));  // open: dp
  Hex_Digit_Display hex_digit_display_24 (.value(alu_2_1_rotate_output_2));  // open: dp
  assign out_17 = sft_out_en ? {alu_2_1_shift_output_2, alu_2_1_shift_output} : 8'bz;  // Controlled_Buffer controlled_buffer_10
  Hex_Digit_Display hex_digit_display_25 (.value(alu_2_1_rotate_output));  // open: dp
  assign out_49 = in_2 ? sram_rd : 1'bz;  // Controlled_Buffer controlled_buffer_11
  assign out_54 = in_2 ? a_in : 1'bz;  // Controlled_Buffer controlled_buffer_12
  assign out_55 = in_2 ? a_out : 1'bz;  // Controlled_Buffer controlled_buffer_13
  assign out_56 = in_2 ? b_in : 1'bz;  // Controlled_Buffer controlled_buffer_14
  assign out_57 = in_2 ? alu_out : 1'bz;  // Controlled_Buffer controlled_buffer_15
  assign out_58 = in_2 ? alu_sub : 1'bz;  // Controlled_Buffer controlled_buffer_16
  assign out_7 = in_2 ? reg_a_out_en : 1'bz;  // Controlled_Buffer controlled_buffer_17
  assign out_8 = in_2 ? sft_in : 1'bz;  // Controlled_Buffer controlled_buffer_18
  assign out_9 = in_2 ? rot_in : 1'bz;  // Controlled_Buffer controlled_buffer_19
  assign out_10 = in_2 ? sft_dir : 1'bz;  // Controlled_Buffer controlled_buffer_20
  assign out_11 = in_2 ? rot_dir : 1'bz;  // Controlled_Buffer controlled_buffer_21
  assign out_15 = in_2 ? alu_out_en : 1'bz;  // Controlled_Buffer controlled_buffer_22
  assign out_16 = in_2 ? sft_am : 1'bz;  // Controlled_Buffer controlled_buffer_23
  assign out_18 = in_2 ? rot_am : 1'bz;  // Controlled_Buffer controlled_buffer_24
  assign out_19 = in_2 ? new_reg_in : 1'bz;  // Controlled_Buffer controlled_buffer_25
  assign out_20 = in_2 ? new_reg_out : 1'bz;  // Controlled_Buffer controlled_buffer_26
  assign out_21 = in_2 ? sft_out_en : 1'bz;  // Controlled_Buffer controlled_buffer_27
  assign out_26 = in_2 ? rot_out_en : 1'bz;  // Controlled_Buffer controlled_buffer_28
  assign out_31 = in_2 ? sft_out : 1'bz;  // Controlled_Buffer controlled_buffer_29
  assign out_35 = in_2 ? rot_out : 1'bz;  // Controlled_Buffer controlled_buffer_30
  assign out_41 = in_2 ? sft_reg_in_en : 1'bz;  // Controlled_Buffer controlled_buffer_31
  assign out_45 = in_2 ? rot_reg_in_en : 1'bz;  // Controlled_Buffer controlled_buffer_32
  assign out_47 = in_2 ? pc_en : 1'bz;  // Controlled_Buffer controlled_buffer_33
  assign out_48 = in_2 ? pc_out : 1'bz;  // Controlled_Buffer controlled_buffer_34
  assign out_50 = in_2 ? sram_wr : 1'bz;  // Controlled_Buffer controlled_buffer_35
  assign out_51 = in_2 ? mar_in_en : 1'bz;  // Controlled_Buffer controlled_buffer_36
  assign out_59 = in_2 ? ins_reg_in_en : 1'bz;  // Controlled_Buffer controlled_buffer_37
  assign out_60 = in_2 ? ins_reg_out_en : 1'bz;  // Controlled_Buffer controlled_buffer_38
  // Pins of 1 and 4 bits meet at out_39

  assign out_37 = out_17[3:0];
  assign out_46[3] = 1'b0;

  // Other names for the same wires on the sheet: address[3:0] = out_52; b_out = in_6; clk = in_3; data_load_en = in_1;
  //   debug = in_5; debug_data[7:0] = out_53; en = in_2; pc_reset = in_4

  // Notes on the sheet:
  //   Data loading
  //   Clock
  //   Operation
endmodule

module alu_2 (
  input  [7:0] reg_a,
  input  alu_out,
  input  alu_sub,
  input  [7:0] reg_b,
  input  [7:0] shift_in_data,
  input  shift_direction,
  input  sft_reg_in_en,
  input  [3:0] shift_amount,
  input  sft_out,
  input  clk,
  input  [7:0] rotate_in_data,
  input  rotate_direction,
  input  rot_reg_in_en,
  input  [3:0] rotate_amount,
  input  rot_out,
  output [7:0] alu_output,
  output alu_carry_out,
  output [7:0] shift_output,
  output [7:0] rotate_output
);

  alu alu_1 (
    .alu_in_1(reg_a), .alu_out_en(alu_out), .alu_sub(alu_sub), .alu_in_2(reg_b), .alu_out(alu_output),
    .alu_carry_out(alu_carry_out));
  barrel_shifter barrel_shifter_1 (
    .data(shift_in_data), .direction(shift_direction), .sft_reg_in_en(sft_reg_in_en), .clk(clk),
    .shift_amount(shift_amount), .sft_out(sft_out), .data_out(shift_output));
  total_rotater total_rotater_1 (
    .data(rotate_in_data), .direction(rotate_direction), .rot_reg_in_en(rot_reg_in_en),
    .rotate_amount(rotate_amount), .clk(clk), .rot_out(rot_out), .data_out(rotate_output));
endmodule

module new_reg (
  input  [3:0] reg_in,
  input  reg_in_en,
  input  reg_clk,
  input  reg_out_en,
  output [3:0] reg_int_out,
  output [3:0] reg_out
);

  wire multiplexer_1_out, multiplexer_2_out, multiplexer_3_out, multiplexer_4_out;

  Multiplexer multiplexer_1 (.in0(reg_int_out[0]), .in1(reg_in[3]), .out(multiplexer_1_out), .sel(reg_in_en));
  D_Flip_Flop d_ff_1 (.D(multiplexer_1_out), .clk(reg_clk), .Q(reg_int_out[0]));  // open: Qn, preset, reset
  assign reg_out[3] = reg_out_en ? reg_int_out[0] : 1'bz;  // Controlled_Buffer controlled_buffer_1
  Multiplexer multiplexer_2 (.in0(reg_int_out[2]), .in1(reg_in[2]), .out(multiplexer_2_out), .sel(reg_in_en));
  D_Flip_Flop d_ff_2 (.D(multiplexer_2_out), .clk(reg_clk), .Q(reg_int_out[2]));  // open: Qn, preset, reset
  assign reg_out[2] = reg_out_en ? reg_int_out[2] : 1'bz;  // Controlled_Buffer controlled_buffer_2
  Multiplexer multiplexer_3 (.in0(reg_int_out[1]), .in1(reg_in[1]), .out(multiplexer_3_out), .sel(reg_in_en));
  D_Flip_Flop d_ff_3 (.D(multiplexer_3_out), .clk(reg_clk), .Q(reg_int_out[1]));  // open: Qn, preset, reset
  assign reg_out[1] = reg_out_en ? reg_int_out[1] : 1'bz;  // Controlled_Buffer controlled_buffer_3
  D_Flip_Flop d_ff_4 (.D(multiplexer_4_out), .clk(reg_clk), .Q(reg_int_out[3]));  // open: Qn, preset, reset
  assign reg_out[0] = reg_out_en ? reg_int_out[3] : 1'bz;  // Controlled_Buffer controlled_buffer_4
  Multiplexer multiplexer_4 (.in0(reg_int_out[3]), .in1(reg_in[0]), .out(multiplexer_4_out), .sel(reg_in_en));
endmodule

module cntr (
  input  pc_en,
  input  clk,
  input  pc_reset,
  input  pc_out_en,
  output [3:0] pc_value,
  output [3:0] pc_output
);

  wire j_k_ff_2_qn, j_k_ff_3_qn, j_k_ff_4_qn;

  J_K_Flip_Flop j_k_ff_1 (
    .J(pc_en), .K(pc_en), .clk(j_k_ff_2_qn), .Q(pc_value[3]), .reset(pc_reset));  // open: Qn, preset
  J_K_Flip_Flop j_k_ff_2 (
    .J(pc_en), .K(pc_en), .clk(j_k_ff_3_qn), .Q(pc_value[2]), .Qn(j_k_ff_2_qn), .reset(pc_reset));  // open: preset
  J_K_Flip_Flop j_k_ff_3 (
    .J(pc_en), .K(pc_en), .clk(j_k_ff_4_qn), .Q(pc_value[1]), .Qn(j_k_ff_3_qn), .reset(pc_reset));  // open: preset
  J_K_Flip_Flop j_k_ff_4 (
    .J(pc_en), .K(pc_en), .clk(clk), .Q(pc_value[0]), .Qn(j_k_ff_4_qn), .reset(pc_reset));  // open: preset
  assign pc_output = pc_out_en ? pc_value : 4'bz;  // Controlled_Buffer controlled_buffer_1

  // Notes on the sheet:
  //   Clock
  //   Reset
  //   Output Control
  //   Count Control
  //   Counter Output
endmodule

module left_barrel_shifter (
  input  [7:0] data,
  input  [2:0] shift_amount,
  output [7:0] out_3
);

  wire multiplexer_1_out, multiplexer_2_out, multiplexer_3_out, multiplexer_4_out, multiplexer_5_out,
       multiplexer_6_out, multiplexer_7_out, multiplexer_8_out, multiplexer_9_out, multiplexer_10_out,
       multiplexer_11_out, multiplexer_12_out, multiplexer_13_out, multiplexer_14_out, multiplexer_15_out,
       multiplexer_16_out;

  Multiplexer multiplexer_1 (.in0(data[7]), .in1(data[6]), .out(multiplexer_1_out), .sel(shift_amount[0]));
  Multiplexer multiplexer_2 (.in0(data[6]), .in1(data[5]), .out(multiplexer_2_out), .sel(shift_amount[0]));
  Multiplexer multiplexer_3 (.in0(data[5]), .in1(data[4]), .out(multiplexer_3_out), .sel(shift_amount[0]));
  Multiplexer multiplexer_4 (.in0(data[4]), .in1(data[3]), .out(multiplexer_4_out), .sel(shift_amount[0]));
  Multiplexer multiplexer_5 (.in0(data[3]), .in1(data[2]), .out(multiplexer_5_out), .sel(shift_amount[0]));
  Multiplexer multiplexer_6 (.in0(data[2]), .in1(data[1]), .out(multiplexer_6_out), .sel(shift_amount[0]));
  Multiplexer multiplexer_7 (.in0(data[1]), .in1(data[0]), .out(multiplexer_7_out), .sel(shift_amount[0]));
  Multiplexer multiplexer_8 (.in0(data[0]), .in1(1'b0), .out(multiplexer_8_out), .sel(shift_amount[0]));
  Multiplexer multiplexer_9 (
    .in0(multiplexer_1_out), .in1(multiplexer_3_out), .out(multiplexer_9_out), .sel(shift_amount[1]));
  Multiplexer multiplexer_10 (
    .in0(multiplexer_2_out), .in1(multiplexer_4_out), .out(multiplexer_10_out), .sel(shift_amount[1]));
  Multiplexer multiplexer_11 (
    .in0(multiplexer_3_out), .in1(multiplexer_5_out), .out(multiplexer_11_out), .sel(shift_amount[1]));
  Multiplexer multiplexer_12 (
    .in0(multiplexer_4_out), .in1(multiplexer_6_out), .out(multiplexer_12_out), .sel(shift_amount[1]));
  Multiplexer multiplexer_13 (
    .in0(multiplexer_5_out), .in1(multiplexer_7_out), .out(multiplexer_13_out), .sel(shift_amount[1]));
  Multiplexer multiplexer_14 (
    .in0(multiplexer_6_out), .in1(multiplexer_8_out), .out(multiplexer_14_out), .sel(shift_amount[1]));
  Multiplexer multiplexer_15 (.in0(multiplexer_7_out), .in1(1'b0), .out(multiplexer_15_out), .sel(shift_amount[1]));
  Multiplexer multiplexer_16 (.in0(multiplexer_8_out), .in1(1'b0), .out(multiplexer_16_out), .sel(shift_amount[1]));
  Multiplexer multiplexer_17 (.in0(multiplexer_9_out), .in1(multiplexer_13_out), .out(out_3[7]), .sel(shift_amount[2]));
  Multiplexer multiplexer_18 (
    .in0(multiplexer_10_out), .in1(multiplexer_14_out), .out(out_3[6]), .sel(shift_amount[2]));
  Multiplexer multiplexer_19 (
    .in0(multiplexer_11_out), .in1(multiplexer_15_out), .out(out_3[5]), .sel(shift_amount[2]));
  Multiplexer multiplexer_20 (.in0(multiplexer_12_out), .in1(1'b0), .out(out_3[4]), .sel(shift_amount[2]));
  Multiplexer multiplexer_21 (.in0(multiplexer_13_out), .in1(1'b0), .out(out_3[3]), .sel(shift_amount[2]));
  Multiplexer multiplexer_22 (.in0(multiplexer_14_out), .in1(1'b0), .out(out_3[2]), .sel(shift_amount[2]));
  Multiplexer multiplexer_23 (.in0(multiplexer_15_out), .in1(1'b0), .out(out_3[1]), .sel(shift_amount[2]));
  Multiplexer multiplexer_24 (.in0(multiplexer_16_out), .in1(1'b0), .out(out_3[0]), .sel(shift_amount[2]));
endmodule

module reverse_bits (
  input  [7:0] in_1,
  output [7:0] out_2
);


  assign out_2 = {in_1[0], in_1[1], in_1[2], in_1[3], in_1[4], in_1[5], in_1[6], in_1[7]};
endmodule

module barrel_shifter (
  input  [7:0] data,
  input  direction,
  input  sft_reg_in_en,
  input  clk,
  input  [3:0] shift_amount,
  input  sft_out,
  output [7:0] data_out
);

  wire [7:0] multiplexer_1_out, multiplexer_2_out, reverse_bits_1_out_2, reverse_bits_2_out_2,
       sftr_1_shift_output;

  reverse_bits reverse_bits_1 (.in_1(data), .out_2(reverse_bits_1_out_2));
  Multiplexer #(.width(8)) multiplexer_1 (
    .in0(reverse_bits_1_out_2), .in1(data), .out(multiplexer_1_out), .sel(direction));
  sftr sftr_1 (.data(multiplexer_1_out), .shift_amount(shift_amount), .shift_output(sftr_1_shift_output));
  reverse_bits reverse_bits_2 (.in_1(sftr_1_shift_output), .out_2(reverse_bits_2_out_2));
  Multiplexer #(.width(8)) multiplexer_2 (
    .in0(reverse_bits_2_out_2), .in1(sftr_1_shift_output), .out(multiplexer_2_out), .sel(direction));
  reg_gp reg_gp_1 (
    .reg_in(multiplexer_2_out), .reg_in_en(sft_reg_in_en), .reg_clk(clk), .reg_out_en(sft_out),
    .reg_int_out(data_out));  // open: reg_out
endmodule

module rotater (
  input  [7:0] data,
  input  [3:0] rotate_amount,
  output [7:0] rot_output
);

  wire multiplexer_1_out, multiplexer_2_out, multiplexer_3_out, multiplexer_4_out, multiplexer_5_out,
       multiplexer_6_out, multiplexer_7_out, multiplexer_8_out, multiplexer_9_out, multiplexer_10_out,
       multiplexer_11_out, multiplexer_12_out, multiplexer_13_out, multiplexer_14_out, multiplexer_15_out,
       multiplexer_16_out;

  Multiplexer multiplexer_1 (.in0(data[7]), .in1(data[6]), .out(multiplexer_1_out), .sel(rotate_amount[0]));
  Multiplexer multiplexer_2 (.in0(data[6]), .in1(data[5]), .out(multiplexer_2_out), .sel(rotate_amount[0]));
  Multiplexer multiplexer_3 (.in0(data[5]), .in1(data[4]), .out(multiplexer_3_out), .sel(rotate_amount[0]));
  Multiplexer multiplexer_4 (.in0(data[4]), .in1(data[3]), .out(multiplexer_4_out), .sel(rotate_amount[0]));
  Multiplexer multiplexer_5 (.in0(data[3]), .in1(data[2]), .out(multiplexer_5_out), .sel(rotate_amount[0]));
  Multiplexer multiplexer_6 (.in0(data[2]), .in1(data[1]), .out(multiplexer_6_out), .sel(rotate_amount[0]));
  Multiplexer multiplexer_7 (.in0(data[1]), .in1(data[0]), .out(multiplexer_7_out), .sel(rotate_amount[0]));
  Multiplexer multiplexer_8 (.in0(data[0]), .in1(data[7]), .out(multiplexer_8_out), .sel(rotate_amount[0]));
  Multiplexer multiplexer_9 (
    .in0(multiplexer_1_out), .in1(multiplexer_3_out), .out(multiplexer_9_out), .sel(rotate_amount[1]));
  Multiplexer multiplexer_10 (
    .in0(multiplexer_2_out), .in1(multiplexer_4_out), .out(multiplexer_10_out), .sel(rotate_amount[1]));
  Multiplexer multiplexer_11 (
    .in0(multiplexer_3_out), .in1(multiplexer_5_out), .out(multiplexer_11_out), .sel(rotate_amount[1]));
  Multiplexer multiplexer_12 (
    .in0(multiplexer_4_out), .in1(multiplexer_6_out), .out(multiplexer_12_out), .sel(rotate_amount[1]));
  Multiplexer multiplexer_13 (
    .in0(multiplexer_5_out), .in1(multiplexer_7_out), .out(multiplexer_13_out), .sel(rotate_amount[1]));
  Multiplexer multiplexer_14 (
    .in0(multiplexer_6_out), .in1(multiplexer_8_out), .out(multiplexer_14_out), .sel(rotate_amount[1]));
  Multiplexer multiplexer_15 (
    .in0(multiplexer_7_out), .in1(multiplexer_1_out), .out(multiplexer_15_out), .sel(rotate_amount[1]));
  Multiplexer multiplexer_16 (
    .in0(multiplexer_8_out), .in1(multiplexer_2_out), .out(multiplexer_16_out), .sel(rotate_amount[1]));
  Multiplexer multiplexer_17 (
    .in0(multiplexer_9_out), .in1(multiplexer_13_out), .out(rot_output[7]), .sel(rotate_amount[2]));
  Multiplexer multiplexer_18 (
    .in0(multiplexer_10_out), .in1(multiplexer_14_out), .out(rot_output[6]), .sel(rotate_amount[2]));
  Multiplexer multiplexer_19 (
    .in0(multiplexer_11_out), .in1(multiplexer_15_out), .out(rot_output[5]), .sel(rotate_amount[2]));
  Multiplexer multiplexer_20 (
    .in0(multiplexer_12_out), .in1(multiplexer_16_out), .out(rot_output[4]), .sel(rotate_amount[2]));
  Multiplexer multiplexer_21 (
    .in0(multiplexer_13_out), .in1(multiplexer_9_out), .out(rot_output[3]), .sel(rotate_amount[2]));
  Multiplexer multiplexer_22 (
    .in0(multiplexer_14_out), .in1(multiplexer_10_out), .out(rot_output[2]), .sel(rotate_amount[2]));
  Multiplexer multiplexer_23 (
    .in0(multiplexer_15_out), .in1(multiplexer_11_out), .out(rot_output[1]), .sel(rotate_amount[2]));
  Multiplexer multiplexer_24 (
    .in0(multiplexer_16_out), .in1(multiplexer_12_out), .out(rot_output[0]), .sel(rotate_amount[2]));
  // also tied to GND on the sheet: rotate_amount[3]
endmodule

module sftr (
  input  [7:0] data,
  input  [3:0] shift_amount,
  output [7:0] shift_output
);

  wire multiplexer_1_out, multiplexer_2_out, multiplexer_3_out, multiplexer_4_out, multiplexer_5_out,
       multiplexer_6_out, multiplexer_7_out, multiplexer_8_out, multiplexer_9_out, multiplexer_10_out,
       multiplexer_11_out, multiplexer_12_out, multiplexer_13_out, multiplexer_14_out, multiplexer_15_out,
       multiplexer_16_out;

  Multiplexer multiplexer_1 (.in0(data[7]), .in1(data[6]), .out(multiplexer_1_out), .sel(shift_amount[0]));
  Multiplexer multiplexer_2 (.in0(data[6]), .in1(data[5]), .out(multiplexer_2_out), .sel(shift_amount[0]));
  Multiplexer multiplexer_3 (.in0(data[5]), .in1(data[4]), .out(multiplexer_3_out), .sel(shift_amount[0]));
  Multiplexer multiplexer_4 (.in0(data[4]), .in1(data[3]), .out(multiplexer_4_out), .sel(shift_amount[0]));
  Multiplexer multiplexer_5 (.in0(data[3]), .in1(data[2]), .out(multiplexer_5_out), .sel(shift_amount[0]));
  Multiplexer multiplexer_6 (.in0(data[2]), .in1(data[1]), .out(multiplexer_6_out), .sel(shift_amount[0]));
  Multiplexer multiplexer_7 (.in0(data[1]), .in1(data[0]), .out(multiplexer_7_out), .sel(shift_amount[0]));
  Multiplexer multiplexer_8 (.in0(data[0]), .in1(multiplexer_8_out), .out(multiplexer_8_out), .sel(shift_amount[0]));
  Multiplexer multiplexer_9 (
    .in0(multiplexer_1_out), .in1(multiplexer_3_out), .out(multiplexer_9_out), .sel(shift_amount[1]));
  Multiplexer multiplexer_10 (
    .in0(multiplexer_2_out), .in1(multiplexer_4_out), .out(multiplexer_10_out), .sel(shift_amount[1]));
  Multiplexer multiplexer_11 (
    .in0(multiplexer_3_out), .in1(multiplexer_5_out), .out(multiplexer_11_out), .sel(shift_amount[1]));
  Multiplexer multiplexer_12 (
    .in0(multiplexer_4_out), .in1(multiplexer_6_out), .out(multiplexer_12_out), .sel(shift_amount[1]));
  Multiplexer multiplexer_13 (
    .in0(multiplexer_5_out), .in1(multiplexer_7_out), .out(multiplexer_13_out), .sel(shift_amount[1]));
  Multiplexer multiplexer_14 (
    .in0(multiplexer_6_out), .in1(multiplexer_8_out), .out(multiplexer_14_out), .sel(shift_amount[1]));
  Multiplexer multiplexer_15 (
    .in0(multiplexer_7_out), .in1(multiplexer_8_out), .out(multiplexer_15_out), .sel(shift_amount[1]));
  Multiplexer multiplexer_16 (
    .in0(multiplexer_8_out), .in1(multiplexer_8_out), .out(multiplexer_16_out), .sel(shift_amount[1]));
  Multiplexer multiplexer_17 (
    .in0(multiplexer_9_out), .in1(multiplexer_13_out), .out(shift_output[7]), .sel(shift_amount[2]));
  Multiplexer multiplexer_18 (
    .in0(multiplexer_10_out), .in1(multiplexer_14_out), .out(shift_output[6]), .sel(shift_amount[2]));
  Multiplexer multiplexer_19 (
    .in0(multiplexer_11_out), .in1(multiplexer_15_out), .out(shift_output[5]), .sel(shift_amount[2]));
  Multiplexer multiplexer_20 (
    .in0(multiplexer_12_out), .in1(multiplexer_16_out), .out(shift_output[4]), .sel(shift_amount[2]));
  Multiplexer multiplexer_21 (
    .in0(multiplexer_13_out), .in1(multiplexer_8_out), .out(shift_output[3]), .sel(shift_amount[2]));
  Multiplexer multiplexer_22 (
    .in0(multiplexer_14_out), .in1(multiplexer_8_out), .out(shift_output[2]), .sel(shift_amount[2]));
  Multiplexer multiplexer_23 (
    .in0(multiplexer_15_out), .in1(multiplexer_8_out), .out(shift_output[1]), .sel(shift_amount[2]));
  Multiplexer multiplexer_24 (
    .in0(multiplexer_16_out), .in1(multiplexer_8_out), .out(shift_output[0]), .sel(shift_amount[2]));
  // also tied to GND on the sheet: {multiplexer_8_out, shift_amount[3]}
endmodule

module total_rotater (
  input  [7:0] data,
  input  direction,
  input  rot_reg_in_en,
  input  [3:0] rotate_amount,
  input  clk,
  input  rot_out,
  output [7:0] data_out
);

  wire [7:0] multiplexer_1_out, multiplexer_2_out, reverse_bits_1_out_2, reverse_bits_2_out_2,
       rotater_1_rot_output;

  reverse_bits reverse_bits_1 (.in_1(data), .out_2(reverse_bits_1_out_2));
  Multiplexer #(.width(8)) multiplexer_1 (
    .in0(reverse_bits_1_out_2), .in1(data), .out(multiplexer_1_out), .sel(direction));
  rotater rotater_1 (.data(multiplexer_1_out), .rotate_amount(rotate_amount), .rot_output(rotater_1_rot_output));
  reverse_bits reverse_bits_2 (.in_1(rotater_1_rot_output), .out_2(reverse_bits_2_out_2));
  Multiplexer #(.width(8)) multiplexer_2 (
    .in0(reverse_bits_2_out_2), .in1(rotater_1_rot_output), .out(multiplexer_2_out), .sel(direction));
  reg_gp reg_gp_1 (
    .reg_in(multiplexer_2_out), .reg_in_en(rot_reg_in_en), .reg_clk(clk), .reg_out_en(rot_out),
    .reg_int_out(data_out));  // open: reg_out
endmodule
